# Fritzing sketch ethanol-sensor-standalone2 (saved by Fritzing 0.9.4)
circuit board: 5cm x 2.5cm
breadboards: 1

parts:
  ATMega328pu = atmega328 [package=dip]
  10k = Resistor [tolerance=±5% resistance=10k package=THT]
  7805 = Voltage Regulator - 5V [package="TO220 [THT]"]
  16mhz = Crystal [frequency="16 Mhz" package=THT]
  22pF = Ceramic Capacitor [capacitance=22pF package="200 mil [THT, multilayer]"]
  22pF_2 = Ceramic Capacitor [capacitance=22pF package="200 mil [THT, multilayer]"]
  VCC_GND_A4_A5 = female pin header, 4 pins [form="♀ (female)"]
  1uF = Ceramic Capacitor [capacitance=0.1µF voltage=50V package="200 mil [THT, multilayer]"]
  0_1uF = Ceramic Capacitor [capacitance=0.1µF voltage=50V package="200 mil [THT, multilayer]"]
  22uF = Ceramic Capacitor [capacitance=0.22mF voltage=50V package="200 mil [THT, multilayer]"]
  4_7k = Resistor [tolerance=±1% resistance=4.7k package=THT]
  3_9k = Resistor [tolerance=±1% resistance=4.7k package=THT]
  J2 = screw terminal, 4 pins

nets:
  N1: ATMega328pu.RESET, 10k.Pin_1
  5v: ATMega328pu.VCC, ATMega328pu.AVCC, 10k.Pin_0, 7805.output_voltage, VCC_GND_A4_A5.pin4, 1uF.1, 4_7k.Pin_1
  GND: ATMega328pu.GND, 7805.GND, 22pF.0, 22pF_2.0, VCC_GND_A4_A5.pin3, 1uF.0, 0_1uF.0, 22uF.1, J2.pin2
  N2: ATMega328pu.XLAT1, 16mhz.pin_1, 22pF.1
  N3: ATMega328pu.XLAT2, 16mhz.pin_0, 22pF_2.1
  Sens In: ATMega328pu.D8, 4_7k.Pin_0, J2.pin3
  N4: ATMega328pu.D10_(PWM), 3_9k.Pin_0
  N5: ATMega328pu.A4, VCC_GND_A4_A5.pin1
  N6: ATMega328pu.A5, VCC_GND_A4_A5.pin2
  VIN: 7805.input_voltage, 22uF.0, J2.pin1
  0-5v Out: 0_1uF.1, 3_9k.Pin_1, J2.pin4

notes:
  Vout EthIN GND  12v
  Aaron S. 2020
  Ethanol Content Controller v0.1
