# Fritzing sketch ethanol-sensor-standalone (saved by Fritzing 0.9.4)
circuit board: 5cm x 4cm
breadboards: 1

parts:
  Part2 = Arduino Nano (Rev3.0) (ICSP)
  4_7k = Resistor [tolerance=±1% resistance=4.7k package=THT]
  GND_VCC_A5_A4 = female pin header, 4 pins [form="♀ (female)"]
  0_1uF = Ceramic Capacitor [capacitance=0.1µF voltage=50V package="200 mil [THT, multilayer]"]
  L7805 = Voltage Regulator [package=78xxl]
  0_22uF = Ceramic Capacitor [capacitance=0.22mF voltage=50V package="200 mil [THT, multilayer]"]
  3_9k = Resistor [tolerance=±1% resistance=4.7k package=THT]
  0_1uF_2 = Ceramic Capacitor [capacitance=0.1µF voltage=50V package="200 mil [THT, multilayer]"]
  12V_GND_ETH_Vout = screw terminal, 4 pins

nets:
  GND: Part2.GND, GND_VCC_A5_A4.pin4
  N1: Part2.D8, 4_7k.Pin_0, 12V_GND_ETH_Vout.pin2
  N2: Part2.D11/MOSI, 3_9k.Pin_0
  VIN: Part2.VIN, Part2.5V, 4_7k.Pin_1, GND_VCC_A5_A4.pin3, 0_1uF.0, L7805.OUT
  N3: Part2.A5, GND_VCC_A5_A4.pin2
  N4: Part2.A4, GND_VCC_A5_A4.pin1
  N5: L7805.IN, 0_22uF.1, 12V_GND_ETH_Vout.pin4
  N6: 3_9k.Pin_1, 0_1uF_2.1, 12V_GND_ETH_Vout.pin1

notes:
  DetonationEMS Ethanol Content System
  12V GND ETH Vout
  Aaron S.
