# Fritzing sketch v0.0.1 (0.96) (saved by Fritzing 0.9.4)
circuit board: 5cm x 2.5cm
breadboards: 1

parts:
  Part2 = Arduino Nano (Rev3.0) (ICSP)
  R1_4_7k = Resistor [tolerance=±5% resistance=4.7k package=THT]
  (OLED)_GND_VCC_A5_A4 = female pin header, 4 pins [form="♀ (female)"]
  12V_GND_IN = female pin header, 3 pins [form="♀ (female)"]

nets:
  GND: Part2.GND, (OLED)_GND_VCC_A5_A4.pin4, 12V_GND_IN.pin2
  N1: Part2.D8, R1_4_7k.Pin_0, 12V_GND_IN.pin3
  N2: Part2.VIN, 12V_GND_IN.pin1
  N3: Part2.5V, R1_4_7k.Pin_1, (OLED)_GND_VCC_A5_A4.pin3
  N4: Part2.A5, (OLED)_GND_VCC_A5_A4.pin2
  N5: Part2.A4, (OLED)_GND_VCC_A5_A4.pin1

notes:
  DetonationEMS Ethanol Display v0.0.1 -  Aaron S. 2019
  IN GND 12V
  A4 A5 VCC GND
