# Fritzing sketch v0.0.2 (128X64) (saved by Fritzing 0.9.4)
circuit board: 5cm x 2.5cm
breadboards: 1

parts:
  R1_4_7k = Resistor [tolerance=±5% resistance=4.7k package=THT]
  IN_GND_12V = female pin header, 3 pins [form="♀ (female)"]
  OLED1 = OLED 128x32 I2C Monochrome Display
  Part2 = Arduino Nano (Rev3.0)

nets:
  N1: R1_4_7k.Pin_0, IN_GND_12V.pin3, Part2.D8
  VCC: R1_4_7k.Pin_1, OLED1.VCC, Part2.5V
  N2: IN_GND_12V.pin1, Part2.VIN
  GND: IN_GND_12V.pin2, OLED1.GND, Part2.GND
  N3: OLED1.SCK, Part2.A5
  N4: OLED1.SDA, Part2.A4

notes:
  DetonationEMS Ethanol Display v0.0.1
  Aaron S. 2019
